# Fritzing sketch shutterSpeedTester (saved by Fritzing 0.9.3b)
breadboards: 1

parts:
  Composant2 = Arduino Nano (Rev3.0)
  R1 = Resistor [tolerance=±5% resistance=1k package=THT]

nets:
  N1: Composant2.D3, R1.Pin_0
